# Fritzing sketch thermostat_v1 (saved by Fritzing 0.9.3b)

parts:
  Raspberry_Pi_Zero1 = Raspberry Pi Zero
  DS1 = DS18B20 1-Wire Temperature Sensor [part_number=DS18B20]
  R1 = Resistor [tolerance=±5% resistance=4.7 package="2512 [SMD]"]
  KY-1 = Keyes Relay [package=THT]

nets:
  3V3: Raspberry_Pi_Zero1.3v3, Raspberry_Pi_Zero1.3V3, DS1.VDD, R1.Pin_0
  N1: Raspberry_Pi_Zero1.GIPO22, KY-1.signal
  GND: Raspberry_Pi_Zero1.GND, DS1.GND, KY-1.ground
  N2: Raspberry_Pi_Zero1.GIPO23, DS1.DQ, R1.Pin_1
  N3: Raspberry_Pi_Zero1.5V, KY-1.power

notes:
  Caldaia
  Temperatura

custom parts:
  Keyes Relay: The Keyes 5V relay module is suitable for SCM development, home appliance control. It uses a 5V~12V TIL control signal which can control DC / AC signal.
